# Fritzing sketch Pyun2Controller2_ケース内配線 (saved by Fritzing 0.9.2b)
perfboards: 1

parts:
  J1 = double row male pin header, 4 pins [form="♂ (male)"]  # not connected
  J2 = double row male pin header, 4 pins [form="♂ (male)"]
  J3 = double row male pin header, 2 pins [form="♂ (male)"]
  J4 = double row male pin header, 2 pins [form="♂ (male)"]
  R1 = Rotary Potentiometer (Small) [maximum_resistance=100kΩ package=THT]
  R2 = Rotary Potentiometer (Small) [maximum_resistance=100kΩ package=THT]
  R3 = Rotary Potentiometer (Small) [maximum_resistance=100kΩ package=THT]
  U1 = mystery part, 5 pins [chip_label="Analog Pin"]
  U2 = mystery part, 2 pins [chip_label=PWR]
  U3 = mystery part, 6 pins [chip_label="Digital Pin"]

nets:
  N1: J2.pin1, R1.leg1, R2.leg1, R3.leg1
  N2: J2.pin2, R1.leg2, R2.leg2, R3.leg2
  N3: J2.pin3, U2.pin1
  N4: J2.pin4, U2.pin2
  N5: J3.pin1, U3.pin5
  N6: J3.pin2, U3.pin6
  N7: J4.pin1, U1.pin4
  N8: J4.pin2, U1.pin5
  N9: R1.wiper, U1.pin1
  N10: R2.wiper, U1.pin2
  N11: R3.wiper, U1.pin3

notes:
  Controller Board
